# Fritzing sketch Systeme-de-telesurveillance (saved by Fritzing 0.9.3b)

parts:
  M1 = MAX30102
  Gizwits_WiFi_Witty_ESP-12F1 = Gizwits WiFi Witty ESP-12F
  OLED1 = OLED 128x64 I2C Monochrome Display VDD-GND

nets:
  VIN: M1.VIN, Gizwits_WiFi_Witty_ESP-12F1.VCC, OLED1.VDD
  N1: M1.SCL, Gizwits_WiFi_Witty_ESP-12F1.GPIO5, OLED1.SCK
  N2: M1.SDA, Gizwits_WiFi_Witty_ESP-12F1.GPIO4, OLED1.SDA
  GND: Gizwits_WiFi_Witty_ESP-12F1.GND, OLED1.GND

custom parts:
  MAX30102: Oximeter module using the MAX30102 chip. You may wish to read (and check your module) this post on power problems with these modules: https://reedpaper.wordpress.com/2018/08/22/pulse-oximeter-max30100-max30102-how-to-fix-wrong-board/ . As usual, if you want the mounting holes in pcb, you need to drag a hole over the pad in silkscreen to actually drill the hole (by default they are not drilled)
  OLED 128x64 I2C Monochrome Display VDD-GND: OLED 128x64 I2C Monochrome Display. Note: there are two variants of this part, this one is the VDD GND SCK SDA variant. The other is GND VDD SCK SDA. Make sure you select the part that matches your module as using the incorrect part will probably destroy your module! In addition the mounting holes are marked on silkscreen but not by default drilled. If you want drilled mounting holes, copy a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
